# Fritzing sketch OJT (saved by Fritzing 0.9.5d)

parts:
  U1 = Module 4 Relais 5V [package="Module 4 Relais 5V"]
  A1 = YwRobot Breadboard Power Supply v5
  CPU1 = NodeMCU WROOM ESP 32
  Capacitive_Soil_Moisture_Sensor1 = DFRobot Capacitive Soil Moisture Sensor V1.0 [part_number=SEN0193]
  A2 = terminal block 8position
  Capacitive_Soil_Moisture_Sensor3 = DFRobot Capacitive Soil Moisture Sensor V1.0 [part_number=SEN0193]
  Capacitive_Soil_Moisture_Sensor4 = DFRobot Capacitive Soil Moisture Sensor V1.0 [part_number=SEN0193]
  Capacitive_Soil_Moisture_Sensor2 = DFRobot Capacitive Soil Moisture Sensor V1.0 [part_number=SEN0193]
  Part1 = LCD1602-I2C

nets:
  VCC: U1.VCC, A1.Pin_22, A1.Pin_24, Part1.VCC
  GND: U1.GND, A1.Pin_10, A1.Pin_14, A1.Pin_21, A1.Pin_23, CPU1.pin_15, Capacitive_Soil_Moisture_Sensor1.GND, Capacitive_Soil_Moisture_Sensor3.GND, Capacitive_Soil_Moisture_Sensor4.GND, Capacitive_Soil_Moisture_Sensor2.GND, Part1.GND
  N1: U1.IN1, CPU1.pin_26
  N2: U1.IN2, CPU1.pin_25
  N3: U1.IN3, CPU1.pin_8, CPU1.pin_24, Capacitive_Soil_Moisture_Sensor2.A
  N4: U1.IN4, CPU1.pin_21
  N5: U1.K1-NF, U1.K2-NF, U1.K3-NF, U1.K4-NF, A2.Pin_1, A2.Pin_2, A2.Pin_3, A2.Pin_4, A2.Pin_13, A2.Pin_14, A2.Pin_15, A2.Pin_16
  N6: A1.Pin_1, A1.Pin_2, A1.Pin_17, A1.Pin_18, CPU1.pin_16
  N7: A1.Pin_7, A1.Pin_8
  VCC_2: A1.Pin_9, A1.Pin_11, Capacitive_Soil_Moisture_Sensor1.VCC, Capacitive_Soil_Moisture_Sensor3.VCC, Capacitive_Soil_Moisture_Sensor4.VCC, Capacitive_Soil_Moisture_Sensor2.VCC
  N8: CPU1.pin_5, Capacitive_Soil_Moisture_Sensor4.A
  N9: CPU1.pin_6, Capacitive_Soil_Moisture_Sensor3.A
  N10: CPU1.pin_7, Capacitive_Soil_Moisture_Sensor1.A
  N11: CPU1.pin_27, Part1.SDA
  N12: CPU1.pin_30, Part1.SCL

custom parts:
  Module 4 Relais 5V: Module 4 Relais 5V 4x SPD-06VDC-SD-C
  YwRobot Breadboard Power Supply v5: YwRobot Breadboard Power Supply v5.
  NodeMCU WROOM ESP 32: 30 pol Development Kit
  DFRobot Capacitive Soil Moisture Sensor V1.0: DFRobot Capacitive Soil Moisture Sensor V1.0 This product measures soil moisture levels by capacitive sensing, rather than resistive sensing like other types of moisture sensor. It is made of a corrosion resistant material giving it a long service life. Insert it into soil and impress your friends with the real-time soil moisture data! The product includes an on-board voltage regulator which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
  LCD1602-I2C: A standard character display, usually with 2x16 characters. Comes in many colors with LCM1602 IIC attached.
